// Logisim project Guia_0506.circ as structural Verilog: 1 circuit, main circuit main
module main (
  input  B,
  input  A,
  input  A_2,
  input  B_2,
  output out_5,
  output out_6
);

  wire and_1_out, and_2_out, and_3_out, and_4_out, and_5_out, and_6_out, and_7_out, and_8_out, and_9_out,
       and_10_out, and_11_out, not_1_out, not_2_out, not_3_out, not_4_out, not_5_out, not_6_out, not_7_out,
       not_8_out, not_9_out, not_10_out, not_11_out, not_12_out, not_13_out, not_14_out;

  not not_1 (not_1_out, B);
  not not_2 (not_2_out, A);
  and and_1 (and_1_out, A_2, A_2);
  not not_3 (not_3_out, and_1_out);
  and and_2 (and_2_out, not_3_out, A_2);
  not not_4 (not_4_out, and_2_out);
  and and_3 (and_3_out, not_4_out, not_4_out);
  not not_5 (not_5_out, and_3_out);
  and and_4 (and_4_out, not_5_out, not_5_out);
  not not_6 (not_6_out, and_4_out);
  not not_7 (not_7_out, and_5_out);
  and and_5 (and_5_out, not_1_out, A);
  not not_8 (not_8_out, not_7_out);
  not not_9 (not_9_out, not_10_out);
  and and_6 (and_6_out, B, not_2_out);
  not not_10 (not_10_out, and_6_out);
  and and_7 (and_7_out, A_2, A_2);
  not not_11 (not_11_out, and_7_out);
  and and_8 (and_8_out, A_2, not_11_out);
  not not_12 (not_12_out, and_8_out);
  and and_9 (and_9_out, not_12_out, not_12_out);
  not not_13 (not_13_out, and_9_out);
  and and_10 (and_10_out, not_13_out, not_13_out);
  not not_14 (not_14_out, and_10_out);
  and and_11 (and_11_out, not_6_out, not_14_out);
  not not_15 (out_6, and_11_out);
  or or_1 (out_5, not_8_out, not_9_out);

  assign B_2 = A_2;

  // Notes on the sheet:
  //   0 1 1 0
  //   a xor b = nand
endmodule
