// Logisim project Guia_0507.circ as structural Verilog: 1 circuit, main circuit main
module main (
  input  A,
  input  B,
  output out_3
);

  wire not_1_out, not_2_out, not_3_out, not_4_out, not_6_out, not_7_out, not_8_out, not_10_out, or_1_out,
       or_2_out, or_3_out, or_4_out, or_5_out, or_6_out, or_7_out, or_8_out, or_9_out, or_10_out;

  or or_1 (or_1_out, A, not_2_out);
  not not_1 (not_1_out, or_1_out);
  or or_2 (or_2_out, A, A);
  not not_2 (not_2_out, or_2_out);
  or or_3 (or_3_out, B, not_2_out);
  not not_3 (not_3_out, or_3_out);
  or or_4 (or_4_out, not_1_out, not_3_out);
  not not_4 (not_4_out, or_4_out);
  or or_5 (or_5_out, B, B);
  not not_5 (not_2_out, or_5_out);
  or or_6 (or_6_out, A, not_2_out);
  not not_6 (not_6_out, or_6_out);
  or or_7 (or_7_out, not_6_out, not_10_out);
  not not_7 (not_7_out, or_7_out);
  or or_8 (or_8_out, not_4_out, not_7_out);
  not not_8 (not_8_out, or_8_out);
  or or_9 (or_9_out, not_8_out, not_8_out);
  not not_9 (out_3, or_9_out);
  or or_10 (or_10_out, not_2_out, B);
  not not_10 (not_10_out, or_10_out);

  // Notes on the sheet:
  //   ~a xor ~b = nor $1 E E 1
endmodule
