// Logisim project Guia_0501.circ as structural Verilog: 1 circuit, main circuit main
module main (
  input  B,
  input  A,
  output out_3
);

  wire not_1_out, not_2_out, not_3_out, or_1_out, or_2_out, or_3_out, or_4_out;

  or or_1 (or_1_out, A, A);
  not not_1 (not_1_out, or_1_out);
  or or_2 (or_2_out, B, B);
  or or_3 (or_3_out, not_1_out, not_1_out);
  not not_2 (not_2_out, or_3_out);
  not not_3 (not_3_out, or_2_out);
  not not_4 (out_3, or_4_out);
  or or_4 (or_4_out, not_3_out, not_2_out);
endmodule
