// Logisim project Guia_0508.circ as structural Verilog: 1 circuit, main circuit main
module main (
  input  B,
  input  A,
  input  A_2,
  input  B_2,
  input  in_5,
  output out_6,
  output out_7,
  output out_8
);

  wire and_1_out, and_2_out, and_3_out, and_4_out, and_5_out, and_6_out, not_1_out, not_2_out, not_3_out,
       not_4_out, not_5_out, not_6_out, not_8_out, or_1_out;

  not not_1 (not_1_out, B);
  not not_2 (not_2_out, A);
  and and_1 (and_1_out, A_2, A_2);
  not not_3 (not_3_out, and_1_out);
  and and_2 (and_2_out, not_8_out, not_8_out);
  and and_3 (and_3_out, not_3_out, not_3_out);
  not not_4 (not_4_out, and_2_out);
  not not_5 (not_5_out, and_3_out);
  and and_4 (and_4_out, not_5_out, not_4_out);
  not not_6 (not_6_out, and_4_out);
  not not_7 (out_6, or_1_out);
  or or_1 (or_1_out, not_1_out, not_2_out);
  and and_5 (and_5_out, B_2, B_2);
  not not_8 (not_8_out, and_5_out);
  // AND_Gate and_6 has open pins: out=and_6_out
  not not_9 (out_7, and_6_out);
  // NOT_Gate not_10 is placed but not wired
  // AND_Gate and_7 is placed but not wired
  // AND_Gate and_8 is placed but not wired
  // OR_Gate or_2 is placed but not wired
  // OR_Gate or_3 is placed but not wired
  // NOT_Gate not_11 is placed but not wired
  // OR_Gate or_4 is placed but not wired
  // OR_Gate or_5 is placed but not wired
  // NOT_Gate not_12 is placed but not wired
  // NOT_Gate not_13 is placed but not wired

  // Notes on the sheet:
  //   ~(~a | ~b) = nand
  //   0 0 0 1 
endmodule
