// Logisim project Guia1702.circ as structural Verilog: 1 circuit, main circuit main
module main (
  input  in_1,
  input  in_2,
  input  in_3,
  input  in_4,
  input  in_5,
  input  in_6,
  output out_7,
  output out_8,
  output out_9
);

  wire clock_1_out;

  Clock clock_1 (.out(clock_1_out));
  J_K_Flip_Flop j_k_ff_1 (.J(in_1), .clk(clock_1_out), .K(in_2), .Q(out_7));  // open: Qn, preset, reset
  J_K_Flip_Flop j_k_ff_2 (.J(in_3), .clk(clock_1_out), .K(in_5), .Q(out_8));  // open: Qn, preset, reset
  J_K_Flip_Flop j_k_ff_3 (.J(in_4), .clk(clock_1_out), .K(in_6), .Q(out_9));  // open: Qn, preset, reset

  // Notes on the sheet:
  //   Ja
  //   Jb
  //   Jc
endmodule
