// Logisim project Guia1704.circ as structural Verilog: 1 circuit, main circuit main
module main (
  input  in_1,
  output out_2,
  output out_3,
  output out_4
);

  wire clock_1_out, t_ff_4_q;

  Clock clock_1 (.out(clock_1_out));
  T_Flip_Flop t_ff_1 (.clk(clock_1_out), .T(in_1), .Q(out_2));  // open: Qn, preset, reset
  T_Flip_Flop t_ff_2 (.clk(out_2), .T(in_1), .Q(out_3));  // open: Qn, preset, reset
  T_Flip_Flop t_ff_3 (.clk(out_3), .T(in_1), .Q(out_4));  // open: Qn, preset, reset
  T_Flip_Flop t_ff_4 (.clk(out_4), .T(in_1), .Q(t_ff_4_q));  // open: Qn, preset, reset
  T_Flip_Flop t_ff_5 (.clk(t_ff_4_q), .T(in_1));  // open: Q, Qn, preset, reset
endmodule
