// Logisim project Preparacao_0103.circ as structural Verilog: 1 circuit, main circuit main
module main (
  input  A,
  input  B,
  input  C,
  output out_4
);

  wire multiplexer_1_out, not_1_out, not_2_out, not_3_out;

  Multiplexer #(.enable("false")) multiplexer_1 (.in0(A), .in1(B), .out(multiplexer_1_out), .sel(C));
  not not_1 (not_1_out, A);
  Multiplexer #(.enable("false")) multiplexer_2 (.in0(not_1_out), .in1(not_2_out), .out(C), .sel(C));
  not not_2 (not_2_out, B);
  Multiplexer #(.enable("false")) multiplexer_3 (.in0(multiplexer_1_out), .in1(C), .out(out_4), .sel(not_3_out));
  not not_3 (not_3_out, C);

  // Notes on the sheet:
  //   C'A + CB
endmodule
