// Logisim project Preparacao_0102.circ as structural Verilog: 1 circuit, main circuit main
module main (
  input  X,
  input  Y,
  output out_3
);

  wire and_1_out, not_1_out, not_2_out, not_3_out, or_1_out;

  not not_1 (not_1_out, X);
  not not_2 (not_2_out, Y);
  and and_1 (and_1_out, not_1_out, Y);
  not not_3 (not_3_out, or_1_out);
  or or_1 (or_1_out, X, not_2_out);
  and and_2 (out_3, and_1_out, not_3_out);
endmodule
