// Logisim project Preparacao_0105.circ as structural Verilog: 1 circuit, main circuit main
module main (
  input  A,
  input  B,
  output out_3
);

  wire not_1_out, not_2_out, not_3_out, or_1_out, or_2_out, xor_1_out;

  not not_1 (not_1_out, A);
  not not_2 (not_2_out, B);
  not not_3 (not_3_out, or_1_out);
  or or_1 (or_1_out, not_1_out, not_2_out);
  xor xor_1 (xor_1_out, A, B);
  or or_2 (or_2_out, not_3_out, xor_1_out);
  not not_4 (out_3, or_2_out);
endmodule
