// Logisim project Preparacao_0204_a.circ as structural Verilog: 1 circuit, main circuit main
module main (
  input  a,
  input  b,
  output out_3
);

  wire not_1_out;

  not not_1 (not_1_out, a);
  and and_1 (out_3, not_1_out, b);

  // Notes on the sheet:
  //   DA
endmodule
