// Logisim project Preparacao_0204_b.circ as structural Verilog: 1 circuit, main circuit main
module main (
  input  a,
  input  b,
  input  c,
  output out_4
);

  wire and_1_out, and_2_out, and_3_out, and_4_out, not_1_out;

  not not_1 (not_1_out, a);
  and and_1 (and_1_out, not_1_out, b);
  and and_2 (and_2_out, and_1_out, c);
  and and_3 (and_3_out, a, b);
  or or_1 (out_4, and_2_out, and_4_out);
  and and_4 (and_4_out, and_3_out, c);

  // Notes on the sheet:
  //   TA
endmodule
