// Logisim project Preparacao_0204_c.circ as structural Verilog: 1 circuit, main circuit main
module main (
  input  a,
  input  b,
  input  in_3,
  input  c,
  input  in_5,
  output out_6,
  output out_7
);

  wire and_1_out, and_2_out, and_3_out, and_4_out, and_5_out, and_6_out, clock_1_out, not_1_out, not_2_out,
       or_1_out;

  and and_1 (and_1_out, a, b);
  and and_2 (and_2_out, a, b);
  not not_1 (not_1_out, a);
  and and_3 (and_3_out, not_1_out, b);
  and and_4 (and_4_out, and_1_out, c);
  not not_2 (not_2_out, c);
  and and_5 (and_5_out, not_2_out, and_2_out);
  and and_6 (and_6_out, and_3_out, c);
  Clock clock_1 (.out(clock_1_out));
  or or_1 (or_1_out, and_5_out, and_6_out);
  S_R_Flip_Flop s_r_ff_1 (
    .S(and_4_out), .clk(clock_1_out), .R(or_1_out), .Q(out_6), .Qn(out_7), .preset(in_3), .reset(in_5));

  // Notes on the sheet:
  //   SbRb
endmodule
