// Logisim project Preparacao_0204_d.circ as structural Verilog: 1 circuit, main circuit main
module main (
  input  a,
  input  b,
  input  c,
  output out_4
);

  wire xnor_1_out;

  xnor xnor_1 (xnor_1_out, a, b);
  and and_1 (out_4, xnor_1_out, c);

  // Notes on the sheet:
  //   TB
endmodule
