// Logisim project atv ac2.circ as structural Verilog
module meia_soma (
  input  in_1,
  input  in_2,
  output out_3,
  output out_4
);

  xor xor_1 (out_3, in_1, in_2);
  and and_1 (out_4, in_2, in_1);
endmodule

module somador_completo (
  input  in_1,
  input  in_2,
  input  in_3,
  output out_4,
  output out_5
);

  wire meia_soma_2_out_3, meia_soma_2_out_4;

  meia_soma meia_soma_1 (.in_1(in_1), .in_2(meia_soma_2_out_3), .out_3(out_4));  // open: out_4
  meia_soma meia_soma_2 (.in_1(in_2), .in_2(in_3), .out_3(meia_soma_2_out_3), .out_4(meia_soma_2_out_4));
  buf or_1 (out_5, meia_soma_2_out_4);  // OR_Gate
endmodule

module somador_de_4_bits (
  input  in_1,
  input  in_2,
  input  in_3,
  input  in_4,
  input  in_5,
  input  in_6,
  input  in_7,
  input  in_8,
  input  in_9,
  output out_10,
  output out_11,
  output out_12,
  output out_13,
  output out_14
);

  wire somador_completo_1_out_5, somador_completo_2_out_5, somador_completo_3_out_5;

  somador_completo somador_completo_1 (
    .in_1(in_1), .in_2(in_2), .in_3(in_3), .out_5(somador_completo_1_out_5), .out_4(out_10));
  somador_completo somador_completo_2 (
    .in_1(somador_completo_1_out_5), .in_2(in_4), .in_3(in_5), .out_5(somador_completo_2_out_5),
    .out_4(out_11));
  somador_completo somador_completo_3 (
    .in_1(somador_completo_2_out_5), .in_2(in_6), .in_3(in_7), .out_5(somador_completo_3_out_5),
    .out_4(out_12));
  somador_completo somador_completo_4 (
    .in_1(somador_completo_3_out_5), .in_2(in_8), .in_3(in_9), .out_5(out_14), .out_4(out_13));
endmodule

module Decodificador (
  input  E3,
  input  E2,
  input  E1,
  input  E0,
  output A,
  output B,
  output C,
  output D,
  output E,
  output F,
  output G
);

  wire and_1_out, and_2_out, and_3_out, and_4_out, and_5_out, and_6_out, and_7_out, and_8_out, and_9_out,
       and_10_out, and_11_out, and_12_out, and_13_out, and_14_out, and_15_out, and_16_out, and_17_out,
       and_18_out, and_19_out, and_20_out, and_21_out, and_22_out, and_23_out, and_24_out, not_1_out,
       not_2_out, not_3_out, not_4_out, not_5_out, not_6_out, not_7_out, not_8_out, not_9_out, not_10_out,
       not_11_out, not_12_out, not_13_out, not_14_out, not_15_out, not_16_out, not_17_out, not_18_out,
       not_19_out, not_20_out, not_21_out, not_22_out, not_23_out, not_24_out, not_25_out, not_26_out,
       not_27_out, not_28_out, not_29_out, not_30_out, not_31_out, not_32_out, not_33_out, not_34_out,
       not_35_out, not_36_out, not_37_out, not_38_out;

  not not_1 (not_1_out, E2);
  not not_2 (not_2_out, E2);
  and and_1 (and_1_out, not_2_out, not_3_out);
  not not_3 (not_3_out, E0);
  not not_4 (not_4_out, E1);
  and and_2 (and_2_out, not_4_out, not_5_out);
  not not_5 (not_5_out, E0);
  not not_6 (not_6_out, E3);
  and and_3 (and_3_out, not_6_out, E1, E0);
  and and_4 (and_4_out, E3, not_7_out, not_8_out);
  not not_7 (not_7_out, E2);
  not not_8 (not_8_out, E1);
  and and_5 (and_5_out, E3, not_9_out);
  not not_9 (not_9_out, E0);
  not not_10 (not_10_out, E1);
  and and_6 (and_6_out, not_10_out, not_11_out);
  not not_11 (not_11_out, E0);
  not not_12 (not_12_out, E3);
  and and_7 (and_7_out, not_12_out, E1, E0);
  not not_13 (not_13_out, E3);
  and and_8 (and_8_out, not_13_out, E2);
  and and_9 (and_9_out, E3, not_14_out, not_15_out);
  not not_14 (not_14_out, E2);
  not not_15 (not_15_out, E1);
  and and_10 (and_10_out, E3, not_16_out);
  not not_16 (not_16_out, E0);
  not not_17 (not_17_out, E3);
  and and_11 (and_11_out, not_17_out, not_18_out);
  not not_18 (not_18_out, E2);
  not not_19 (not_19_out, E2);
  and and_12 (and_12_out, not_19_out, not_20_out);
  not not_20 (not_20_out, E1);
  not not_21 (not_21_out, E3);
  and and_13 (and_13_out, not_21_out, not_22_out, E0);
  not not_22 (not_22_out, E1);
  not not_23 (not_23_out, E3);
  and and_14 (and_14_out, not_23_out, E1, not_24_out);
  not not_24 (not_24_out, E0);
  not not_25 (not_25_out, E3);
  and and_15 (and_15_out, not_25_out, not_26_out, not_27_out);
  not not_26 (not_26_out, E2);
  not not_27 (not_27_out, E1);
  not not_28 (not_28_out, E2);
  and and_16 (and_16_out, not_28_out, not_29_out);
  not not_29 (not_29_out, E0);
  and and_17 (and_17_out, E1, not_30_out);
  not not_30 (not_30_out, E0);
  and and_18 (and_18_out, E3, E1);
  and and_19 (and_19_out, E3, E2);
  not not_31 (not_31_out, E1);
  or or_1 (F, not_31_out, E2, E3);
  not not_32 (not_32_out, E2);
  and and_20 (and_20_out, not_32_out, E0);
  not not_33 (not_33_out, E3);
  and and_21 (and_21_out, not_33_out, E1, not_34_out);
  not not_34 (not_34_out, E0);
  not not_35 (not_35_out, E3);
  and and_22 (and_22_out, not_35_out, E2, not_36_out);
  not not_36 (not_36_out, E1);
  not not_37 (not_37_out, E2);
  and and_23 (and_23_out, E3, not_37_out, not_38_out);
  not not_38 (not_38_out, E1);
  and and_24 (and_24_out, E3, E0);
  or or_2 (A, not_1_out, E0, E1, E3);
  or or_3 (B, and_1_out, and_2_out, and_3_out, and_4_out, and_5_out);
  or or_4 (C, and_6_out, and_7_out, and_8_out, and_9_out, and_10_out);
  or or_5 (D, and_11_out, and_12_out, and_13_out, and_14_out);
  or or_6 (E, and_15_out, and_16_out, and_17_out, and_18_out, and_19_out);
  or or_7 (G, and_20_out, and_21_out, and_22_out, and_23_out, and_24_out);
endmodule
